# Fritzing sketch plano (saved by Fritzing 0.9.3b)
breadboards: 1

parts:
  Componente1 = Arduino Mega 2560 (Rev3)
  R1 = Resistor [tolerance=±5% resistance=220 package="0603 [SMD]"]
  R2 = Resistor [tolerance=±5% resistance=220 package="0603 [SMD]"]
  R3 = Resistor [tolerance=±5% resistance=220 package="0603 [SMD]"]
  LED1 = LED - 3mm [color="Red (633nm)" package="3 mm [THT]"]
  LED2 = LED - 3mm [color="Red (633nm)" package="3 mm [THT]"]
  LED3 = LED - 3mm [color="Red (633nm)" package="3 mm [THT]"]
  SENSOR_PIR = PIR sensor
  SERVO_EJE_X = Basic Servo
  SERVO_EJE_Y = Basic Servo
  SPKR1 = Loudspeaker

nets:
  N1: Componente1.D13_PWM, SERVO_EJE_X.pulse
  N2: Componente1.D12_PWM, SERVO_EJE_Y.pulse
  N3: Componente1.D11_PWM, SENSOR_PIR.SIG
  N4: Componente1.D10_PWM, R1.Pin_1
  N5: Componente1.D9_PWM, R2.Pin_1
  N6: Componente1.D8_PWM, R3.Pin_1
  VCC: Componente1.5V, SENSOR_PIR.VDD, SERVO_EJE_X.vcc, SERVO_EJE_Y.vcc
  GND: Componente1.GND, LED1.cathode, LED2.cathode, LED3.cathode, SENSOR_PIR.GND, SERVO_EJE_X.gnd, SERVO_EJE_Y.gnd, SPKR1.pin1
  N7: R1.Pin_0, LED2.anode
  N8: R2.Pin_0, LED1.anode
  N9: R3.Pin_0, LED3.anode
